// Logisim project s_complexo.circ as structural Verilog: 1 circuit, main circuit main
module main (
  input  Cin,
  input  a1,
  input  b1,
  output out_4,
  output cout
);

  wire and_1_out, and_2_out, xor_1_out;

  and and_1 (and_1_out, b1, a1);
  xor xor_1 (xor_1_out, a1, b1);
  and and_2 (and_2_out, Cin, xor_1_out);
  xor xor_2 (out_4, Cin, xor_1_out);
  xor xor_3 (cout, and_2_out, and_1_out);
endmodule
