// Logisim project conversor7.circ as structural Verilog: 1 circuit, main circuit main
module main (
  input  in_1,
  input  in_2,
  input  in_3,
  output out_4,
  output out_5,
  output out_6,
  output out_7,
  output out_8,
  output out_9,
  output out_10
);

  pA_main main_1 (.in_1(in_1), .in_2(in_2), .in_3(in_3), .out_4(out_4));
  pB_main main_2 (.in_1(in_1), .in_2(in_2), .in_3(in_3), .out_4(out_5));
  pC_main main_3 (.in_1(in_1), .in_2(in_2), .in_3(in_3), .out_4(out_6));
  pD_main main_4 (.in_1(in_1), .in_2(in_2), .in_3(in_3), .out_4(out_7));
  pE_main main_5 (.in_1(in_1), .in_2(in_2), .in_3(in_3), .out_4(out_8));
  pF_main main_6 (.in_1(in_1), .in_2(in_2), .in_3(in_3), .out_4(out_9));
  pG_main main_7 (.in_1(in_1), .in_2(in_2), .in_3(in_3), .out_4(out_10));
endmodule
