// Logisim project somador_tres_bits.circ as structural Verilog: 1 circuit, main circuit main
module main (
  input  a0,
  input  b0,
  input  a1,
  input  b1,
  input  a2,
  input  b2,
  output out_7,
  output out_8,
  output out_9
);

  wire main_1_out_4, main_2_cout;

  s_simples_main main_1 (.a0(a0), .b0(b0), .out_3(out_7), .out_4(main_1_out_4));
  s_complexo_main main_2 (.Cin(main_1_out_4), .a1(a1), .b1(b1), .out_4(out_8), .cout(main_2_cout));
  s_complexo_main main_3 (.Cin(main_2_cout), .a1(a2), .b1(b2), .out_4(out_9));  // open: cout
endmodule
